// Digital circuit Register and ALU.dig as structural Verilog
module Register_and_ALU (
  input  CLK,
  input  [1:0] Read_Register1,
  input  [1:0] Read_Register2,
  input  [1:0] Write_Register,
  input  [7:0] CTRL,
  input  [2:0] Op_Code,
  input  [7:0] Write_Data,
  input  Write_Sel
);

  wire register_file_1_p7, register_file_1_p8;
  wire [7:0] _8bitalu_1_p4, multiplexer_1_out;

  Multiplexer #(.Bits(8)) multiplexer_1 (
    .sel(Write_Sel), .in_0(Write_Data), .in_1(_8bitalu_1_p4), .out(multiplexer_1_out));
  // Register_File register_file_1: pin names not known; wires that end beside it: CLK, Read_Register1, Read_Register2, multiplexer_1_out, Write_Register, CTRL, register_file_1_p7, register_file_1_p8
  // _8BitALU _8bitalu_1: pin names not known; wires that end beside it: register_file_1_p7, Op_Code, register_file_1_p8, _8bitalu_1_p4
endmodule
